# Fritzing sketch Proiect diagrama fara LCD (saved by Fritzing 0.9.3b)
breadboards: 1

parts:
  LED1 = LED - 5mm [color="Red (633nm)" package="5 mm [THT]"]
  Mod1 = KY-012 Active Buzzer Module [package="Breakout board"]
  R1 = Resistor [tolerance=±5% resistance=220 package=THT]
  DHT1 = DHT22 Humidity and Temperature Sensor
  U1 = ESP32-38PinWide [part_number=ESP32-38PinWide]
  Mod2 = KY-018 Photoresistor Module [package="Breakout board"]
  부품3 = FC-28 Soil Hygrometer Module
  부품4 = FC-28 Soil Hygrometer Module - Probe

nets:
  GND: LED1.cathode, DHT1.GND, U1.GND, Mod2.-, 부품3.GND
  N1: LED1.anode, R1.Pin_0
  N2: Mod1.S, U1.GPIO26
  VDD: Mod1.NC, DHT1.VDD, U1.3.3, Mod2.Vin, 부품3.VCC
  N3: R1.Pin_1, U1.GPIO5
  N4: DHT1.DATA, U1.GPIO4, U1.GPIO16
  N5: U1.GPIO34, 부품3.AO
  N6: U1.GPIO35, Mod2.S
  N7: 부품3.POS, 부품4.POS
  N8: 부품3.NEG, 부품4.NEG

custom parts:
  KY-012 Active Buzzer Module: Active Piezoelectric Buzzer Module KY-012, it produces single-tone sound when signal is high. (Special thanks to vanepp for fixing the PCB holes and other errors)
  ESP32-38PinWide: Generic 38-Pin ESP32 with wide format (only access to one side of pins on a breadboard) based on Stephen Lilley's HiLetgo ESP-WROOM-32 ESP32 ESP-32S Development Board.
  KY-018 Photoresistor Module: KY-018 Photoresistor module, used to measure light intensity. It can determine the presence or absence of light.
  FC-28 Soil Hygrometer Module: The FC-28 is a soil hygrometer module that uses the Texas Instruments LM393 comparator chip to provide an analog measurement of soil humidity. The digital output is high when soil moisture is over a certain threshold, as determined by adjusting the potentiometer.
  FC-28 Soil Hygrometer Module - Probe: The FC-28 is a soil hygrometer module that uses the Texas Instruments LM393 comparator chip to provide an analog measurement of soil humidity.
